# Fritzing sketch Arduino Circuit Breadboard (saved by Fritzing 0.9.3b)
breadboards: 1

parts:
  Part1 = Arduino Uno (Rev3) - ICSP
  Muscle_Sensor = Pulse Sensor [package=SIP-3]
  M1 = Dagu DGServo 9g (Pan and tilt) [part_number=RS001B]

nets:
  N1: Part1.A0, Muscle_Sensor.Signal
  VCC: Part1.5V, Muscle_Sensor.VCC, M1.vcc
  N2: Part1.D9_PWM, M1.pulse
  GND: Part1.GND, Muscle_Sensor.GND, M1.gnd

custom parts:
  Pulse Sensor: Pulse Sensor Optical Heart Beat Sensor
